# Fritzing sketch sketch (saved by Fritzing 0.9.3b)

parts:
  Part1 = Arduino Uno (Rev3)
  Power_RGB1 = Prolight RGB 3 Watt Star

nets:
  N1: Part1.A0, Power_RGB1.B+
  N2: Part1.A1, Power_RGB1.G+
  N3: Part1.A2, Power_RGB1.R+
  N4: Part1.GND, Power_RGB1.R-, Power_RGB1.G-, Power_RGB1.B-

notes:
  RGB led (256 colors)
